// Logisim project Decoder (3-8).circ as structural Verilog: 1 circuit, main circuit main
module main (
  input  A2,
  input  A0,
  input  A1,
  output D0,
  output D1,
  output D2,
  output D3,
  output D4,
  output D5,
  output D6,
  output D7
);

  wire not_1_out, not_2_out, not_3_out;

  not not_1 (not_1_out, A2);
  not not_2 (not_2_out, A0);
  not not_3 (not_3_out, A1);
  and and_1 (D0, not_2_out, not_1_out, not_3_out);
  and and_2 (D1, A0, not_1_out, not_3_out);
  and and_3 (D2, not_2_out, not_1_out, A1);
  and and_4 (D3, A0, not_1_out, A1);
  and and_5 (D4, A2, not_2_out, not_3_out);
  and and_6 (D5, A0, A2, not_3_out);
  and and_7 (D6, A1, A2, not_2_out);
  and and_8 (D7, A0, A1, A2);
endmodule
