// Logisim project Decoder(4-16).circ as structural Verilog: 1 circuit, main circuit main
module main (
  input  A3,
  input  A2,
  input  A1,
  input  A0,
  output D0,
  output D1,
  output D2,
  output D3,
  output D4,
  output D5,
  output D6,
  output D7,
  output D8,
  output D9,
  output D10,
  output D11,
  output D12,
  output D13,
  output D14,
  output D15
);

  wire not_1_out, not_2_out, not_3_out, not_4_out;

  not not_1 (not_1_out, A3);
  not not_2 (not_2_out, A2);
  not not_3 (not_3_out, A1);
  not not_4 (not_4_out, A0);
  and and_1 (D0, not_4_out, not_3_out, not_2_out, not_1_out);
  and and_2 (D1, A0, not_3_out, not_2_out, not_1_out);
  and and_3 (D2, A1, not_4_out, not_2_out, not_1_out);
  and and_4 (D3, A0, A1, not_2_out, not_1_out);
  and and_5 (D4, A2, not_4_out, not_3_out, not_1_out);
  and and_6 (D5, A0, A2, not_3_out, not_1_out);
  and and_7 (D6, A1, A2, not_4_out, not_1_out);
  and and_8 (D7, A0, A1, A2, not_1_out);
  and and_9 (D8, A3, not_4_out, not_3_out, not_2_out);
  and and_10 (D9, A0, A3, not_3_out, not_2_out);
  and and_11 (D10, A1, A3, not_4_out, not_2_out);
  and and_12 (D11, A0, A1, A3, not_2_out);
  and and_13 (D12, A2, A3, not_4_out, not_3_out);
  and and_14 (D13, A0, A2, A3, not_3_out);
  and and_15 (D14, A1, A2, A3, not_4_out);
  and and_16 (D15, A0, A1, A2, A3);
endmodule
