// Logisim project Subcircuit .circ as structural Verilog: 2 circuits, main circuit main
module main (
  input  in_1,
  input  in_2,
  input  in_3,
  input  in_4,
  output out_5,
  output out_6,
  output out_7,
  output out_8,
  output out_9,
  output out_10,
  output out_11,
  output out_12,
  output out_13,
  output out_14,
  output out_15,
  output out_16,
  output out_17,
  output out_18,
  output out_19,
  output out_20
);

  Decoder decoder_1 (
    .A3(in_1), .A2(in_2), .A1(in_3), .A0(in_4), .D0(out_5), .D1(out_6), .D2(out_7), .D3(out_8), .D4(out_9),
    .D5(out_10), .D6(out_11), .D7(out_12), .D8(out_13), .D9(out_14), .D10(out_15), .D11(out_16),
    .D12(out_17), .D13(out_18), .D14(out_19), .D15(out_20));
endmodule

module Decoder (
  input  A3,
  input  A2,
  input  A1,
  input  A0,
  output D0,
  output D1,
  output D2,
  output D3,
  output D4,
  output D5,
  output D6,
  output D7,
  output D8,
  output D9,
  output D10,
  output D11,
  output D12,
  output D13,
  output D14,
  output D15
);

  wire not_1_out, not_2_out, not_3_out, not_4_out;

  not not_1 (not_1_out, A3);
  not not_2 (not_2_out, A2);
  not not_3 (not_3_out, A1);
  not not_4 (not_4_out, A0);
  and and_1 (D0, not_4_out, not_3_out, not_2_out, not_1_out);
  and and_2 (D1, A0, not_3_out, not_2_out, not_1_out);
  and and_3 (D2, A1, not_4_out, not_2_out, not_1_out);
  and and_4 (D3, A0, A1, not_2_out, not_1_out);
  and and_5 (D4, A2, not_4_out, not_3_out, not_1_out);
  and and_6 (D5, A0, A2, not_3_out, not_1_out);
  and and_7 (D6, A1, A2, not_4_out, not_1_out);
  and and_8 (D7, A0, A1, A2, not_1_out);
  and and_9 (D8, A3, not_4_out, not_3_out, not_2_out);
  and and_10 (D9, A0, A3, not_3_out, not_2_out);
  and and_11 (D10, A1, A3, not_4_out, not_2_out);
  and and_12 (D11, A0, A1, A3, not_2_out);
  and and_13 (D12, A2, A3, not_4_out, not_3_out);
  and and_14 (D13, A0, A2, A3, not_3_out);
  and and_15 (D14, A1, A2, A3, not_4_out);
  and and_16 (D15, A0, A1, A2, A3);
endmodule
