// Logisim project Lab_2_27502333_Hussain.circ as structural Verilog: 5 circuits, main circuit 8-bit-register
module _8_bit_register (
  input  D0,
  input  D1,
  input  D2,
  input  D3,
  input  D4,
  input  D5,
  input  D6,
  input  D7,
  input  CLOCK,
  output Q0,
  output Q1,
  output Q2,
  output Q3,
  output Q4,
  output Q5,
  output Q6,
  output Q7
);

  _1bitDlatch u_1bitdlatch_1 (.D(D0), .CLOCK(CLOCK), .Q(Q0));
  _1bitDlatch u_1bitdlatch_2 (.D(D1), .CLOCK(CLOCK), .Q(Q1));
  _1bitDlatch u_1bitdlatch_3 (.D(D2), .CLOCK(CLOCK), .Q(Q2));
  _1bitDlatch u_1bitdlatch_4 (.D(D3), .CLOCK(CLOCK), .Q(Q3));
  _1bitDlatch u_1bitdlatch_5 (.D(D4), .CLOCK(CLOCK), .Q(Q4));
  _1bitDlatch u_1bitdlatch_6 (.D(D5), .CLOCK(CLOCK), .Q(Q5));
  _1bitDlatch u_1bitdlatch_7 (.D(D6), .CLOCK(CLOCK), .Q(Q6));
  _1bitDlatch u_1bitdlatch_8 (.D(D7), .CLOCK(CLOCK), .Q(Q7));

  // Notes on the sheet:
  //   1 8-BIT REGISTER
endmodule

module _1bitDlatch (
  input  D,
  input  CLOCK,
  output Q
);

  wire nand_1_out, nand_2_out, nand_4_out;

  nand nand_1 (nand_1_out, D, CLOCK);
  nand nand_2 (nand_2_out, nand_1_out, CLOCK);
  nand nand_3 (Q, nand_1_out, nand_4_out);
  nand nand_4 (nand_4_out, Q, nand_2_out);

  // Notes on the sheet:
  //   D-LATCH
endmodule

module register_bank (
  input  W_nR,
  input  D0,
  input  D1,
  input  D2,
  input  D3,
  input  D4,
  input  D5,
  input  D6,
  input  D7,
  input  CLOCK,
  input  A0,
  input  A1,
  output Q0,
  output Q1,
  output Q2,
  output Q3,
  output Q4,
  output Q5,
  output Q6,
  output Q7
);

  wire and_1_out, and_2_out, and_3_out, and_4_out, multiplexer_1_out, multiplexer_2_out, multiplexer_3_out,
       multiplexer_4_out, multiplexer_5_out, multiplexer_6_out, multiplexer_7_out, multiplexer_8_out,
       n2to4decoder_1_d0, n2to4decoder_1_d1, n2to4decoder_1_d2, n2to4decoder_1_d3, n8_bit_register_1_q0,
       n8_bit_register_1_q1, n8_bit_register_1_q2, n8_bit_register_1_q3, n8_bit_register_1_q4,
       n8_bit_register_1_q5, n8_bit_register_1_q6, n8_bit_register_1_q7, n8_bit_register_2_q0,
       n8_bit_register_2_q1, n8_bit_register_2_q2, n8_bit_register_2_q3, n8_bit_register_2_q5,
       n8_bit_register_2_q6, n8_bit_register_2_q7, n8_bit_register_3_q0, n8_bit_register_3_q1,
       n8_bit_register_3_q2, n8_bit_register_3_q3, n8_bit_register_3_q4, n8_bit_register_3_q6,
       n8_bit_register_3_q7, n8_bit_register_4_q0, n8_bit_register_4_q1, n8_bit_register_4_q2,
       n8_bit_register_4_q3, n8_bit_register_4_q4, n8_bit_register_4_q5, n8_bit_register_4_q6,
       n8_bit_register_4_q7, not_1_out;

  and and_1 (and_1_out, W_nR, n2to4decoder_1_d0, CLOCK);
  and and_2 (and_2_out, W_nR, n2to4decoder_1_d1, CLOCK);
  and and_3 (and_3_out, W_nR, n2to4decoder_1_d2, CLOCK);
  and and_4 (and_4_out, W_nR, n2to4decoder_1_d3, CLOCK);
  _2to4Decoder u_2to4decoder_1 (
    .A0(A0), .A1(A1), .D0(n2to4decoder_1_d0), .D1(n2to4decoder_1_d1), .D2(n2to4decoder_1_d2),
    .D3(n2to4decoder_1_d3));
  _8_bit_register u_8_bit_register_1 (
    .D0(D0), .D1(D1), .D2(D2), .D3(D3), .D4(D4), .D5(D5), .D6(D6), .D7(D7), .CLOCK(and_1_out),
    .Q0(n8_bit_register_1_q0), .Q1(n8_bit_register_1_q1), .Q2(n8_bit_register_1_q2),
    .Q3(n8_bit_register_1_q3), .Q4(n8_bit_register_1_q4), .Q5(n8_bit_register_1_q5),
    .Q6(n8_bit_register_1_q6), .Q7(n8_bit_register_1_q7));
  _8_bit_register u_8_bit_register_2 (
    .D0(D0), .D1(D1), .D2(D2), .D3(D3), .D4(D4), .D5(D5), .D6(D6), .D7(D7), .CLOCK(and_2_out),
    .Q0(n8_bit_register_2_q0), .Q1(n8_bit_register_2_q1), .Q2(n8_bit_register_2_q2),
    .Q3(n8_bit_register_2_q3), .Q4(n8_bit_register_1_q4), .Q5(n8_bit_register_2_q5),
    .Q6(n8_bit_register_2_q6), .Q7(n8_bit_register_2_q7));
  _8_bit_register u_8_bit_register_3 (
    .D0(D0), .D1(D1), .D2(D2), .D3(D3), .D4(D4), .D5(D5), .D6(D6), .D7(D7), .CLOCK(and_3_out),
    .Q0(n8_bit_register_3_q0), .Q1(n8_bit_register_3_q1), .Q2(n8_bit_register_3_q2),
    .Q3(n8_bit_register_3_q3), .Q4(n8_bit_register_3_q4), .Q5(n8_bit_register_2_q5),
    .Q6(n8_bit_register_3_q6), .Q7(n8_bit_register_3_q7));
  _8_bit_register u_8_bit_register_4 (
    .D0(D0), .D1(D1), .D2(D2), .D3(D3), .D4(D4), .D5(D5), .D6(D6), .D7(D7), .CLOCK(and_4_out),
    .Q0(n8_bit_register_4_q0), .Q1(n8_bit_register_4_q1), .Q2(n8_bit_register_4_q2),
    .Q3(n8_bit_register_4_q3), .Q4(n8_bit_register_4_q4), .Q5(n8_bit_register_4_q5),
    .Q6(n8_bit_register_4_q6), .Q7(n8_bit_register_4_q7));
  Multiplexer #(.select(2)) multiplexer_1 (
    .in0(n8_bit_register_1_q0), .in1(n8_bit_register_2_q0), .in2(n8_bit_register_3_q0),
    .in3(n8_bit_register_4_q0), .out(multiplexer_1_out), .sel({A1, A0}));  // open: en
  Multiplexer #(.select(2)) multiplexer_2 (
    .in0(n8_bit_register_1_q4), .in1(n8_bit_register_1_q4), .in2(n8_bit_register_3_q4),
    .in3(n8_bit_register_4_q4), .out(multiplexer_2_out), .sel({A1, A0}));  // open: en
  Multiplexer #(.select(2)) multiplexer_3 (
    .in0(n8_bit_register_1_q1), .in1(n8_bit_register_2_q1), .in2(n8_bit_register_3_q1),
    .in3(n8_bit_register_4_q1), .out(multiplexer_3_out), .sel({A1, A0}));  // open: en
  Multiplexer #(.select(2)) multiplexer_4 (
    .in0(n8_bit_register_1_q5), .in1(n8_bit_register_2_q5), .in2(n8_bit_register_2_q5),
    .in3(n8_bit_register_4_q5), .out(multiplexer_4_out), .sel({A1, A0}));  // open: en
  Multiplexer #(.select(2)) multiplexer_5 (
    .in0(n8_bit_register_1_q2), .in1(n8_bit_register_2_q2), .in2(n8_bit_register_3_q2),
    .in3(n8_bit_register_4_q2), .out(multiplexer_5_out), .sel({A1, A0}));  // open: en
  Multiplexer #(.select(2)) multiplexer_6 (
    .in0(n8_bit_register_1_q6), .in1(n8_bit_register_2_q6), .in2(n8_bit_register_3_q6),
    .in3(n8_bit_register_4_q6), .out(multiplexer_6_out), .sel({A1, A0}));  // open: en
  Multiplexer #(.select(2)) multiplexer_7 (
    .in0(n8_bit_register_1_q3), .in1(n8_bit_register_2_q3), .in2(n8_bit_register_3_q3),
    .in3(n8_bit_register_4_q3), .out(multiplexer_7_out), .sel({A1, A0}));  // open: en
  Multiplexer #(.select(2)) multiplexer_8 (
    .in0(n8_bit_register_1_q7), .in1(n8_bit_register_2_q7), .in2(n8_bit_register_3_q7),
    .in3(n8_bit_register_4_q7), .out(multiplexer_8_out), .sel({A1, A0}));  // open: en
  not not_1 (not_1_out, W_nR);
  and and_5 (Q0, multiplexer_1_out, not_1_out);
  and and_6 (Q1, multiplexer_3_out, not_1_out);
  and and_7 (Q2, multiplexer_5_out, not_1_out);
  and and_8 (Q3, multiplexer_7_out, not_1_out);
  and and_9 (Q4, multiplexer_2_out, not_1_out);
  and and_10 (Q5, multiplexer_4_out, not_1_out);
  and and_11 (Q6, multiplexer_6_out, not_1_out);
  and and_12 (Q7, multiplexer_8_out, not_1_out);

  // Notes on the sheet:
  //   Register Bank Of 4 8-bit Registers
  //   LEFT IS FIRST
  //   RIGHT IS FIRST
endmodule

module memoryChip (
  input  CLOCK,
  input  W_nR,
  input  A1,
  input  A0,
  input  D0,
  input  D1,
  input  D2,
  input  D3,
  input  D4,
  input  D5,
  input  D6,
  input  D7,
  output Q0,
  output Q1,
  output Q2,
  output Q3,
  output Q4,
  output Q5,
  output Q6,
  output Q7
);

  register_bank register_bank_1 (
    .Q0(Q0), .Q1(Q1), .Q2(Q2), .Q3(Q3), .Q4(Q4), .Q5(Q5), .Q6(Q6), .Q7(Q7), .CLOCK(CLOCK), .D0(D0), .D1(D1),
    .D2(D2), .D3(D3), .D4(D4), .D5(D5), .W_nR(W_nR), .D6(D6), .D7(D7), .A1(A1), .A0(A0));

  // Notes on the sheet:
  //   Memory Chip (4 x 8)
endmodule

module _2to4Decoder (
  input  A0,
  input  A1,
  output D0,
  output D1,
  output D2,
  output D3
);

  wire not_1_out, not_2_out;

  not not_1 (not_1_out, A0);
  not not_2 (not_2_out, A1);
  and and_1 (D0, not_1_out, not_2_out);
  and and_2 (D1, A0, not_2_out);
  and and_3 (D2, not_1_out, A1);
  and and_4 (D3, A0, A1);

  // Notes on the sheet:
  //   2 to 4 Decoder
endmodule
